# Fritzing sketch Bindicator Design (saved by Fritzing 0.9.3b)
breadboards: 1

parts:
  ZS-042_RTC1 = ZS-042 RTC Module
  Part1 = Adafruit Metro Without Headers [part_number="Adafruit #2466"]
  LED1 = LED - 5mm [color="Yellow (595nm)" package="5 mm [THT]"]
  LED2 = LED - 5mm [color="Green (555nm)" package="5 mm [THT]"]
  LED3 = LED - 5mm [color="Blue (430nm)" package="5 mm [THT]"]
  LED5 = LED - 5mm [color="Red (633nm)" package="5 mm [THT]"]
  LED6 = LED - 5mm [color="White (4500K)" package="5 mm [THT]"]
  R1 = Resistor [tolerance=±5% resistance=220 package=THT]
  VCC1 = Battery block 9V
  R2 = Resistor [tolerance=±5% resistance=220 package=THT]
  R3 = Resistor [tolerance=±5% resistance=220 package=THT]
  R4 = Resistor [tolerance=±5% resistance=220 package=THT]
  R5 = Resistor [tolerance=±5% resistance=220 package=THT]

nets:
  GND: ZS-042_RTC1.GND, Part1.GND, LED1.cathode, LED2.cathode, LED3.cathode, LED5.cathode, LED6.cathode, VCC1.-
  VCC: ZS-042_RTC1.VCC, Part1.+5V
  N1: ZS-042_RTC1.SDA, Part1.AD4/SDA
  N2: ZS-042_RTC1.SCL, Part1.AD5/SCL
  N3: Part1.MISO, R4.Pin_0
  N4: Part1.MOSI, R5.Pin_0
  N5: Part1.SS, R3.Pin_0
  N6: Part1.IO9, R2.Pin_0
  N7: Part1.IO8, R1.Pin_0
  N8: Part1.VIN, VCC1.+
  N9: LED1.anode, R5.Pin_1
  N10: LED2.anode, R4.Pin_1
  N11: LED3.anode, R2.Pin_1
  N12: LED5.anode, R3.Pin_1
  N13: LED6.anode, R1.Pin_1

custom parts:
  Adafruit Metro Without Headers: We sure love the ATmega328 here at Adafruit, and we use them a lot for our own projects. The processor has plenty of GPIO, Analog inputs, hardware UART SPI and I2C, timers and PWM galore - just enough for most simple projects. When we need to go small, we use a Pro Trinket 3V or 5V, but when size isn't as much of a concern, and a USB-serial converter is required, we reach for an Adafruit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
