# Fritzing sketch Bindicator PCB (saved by Fritzing 0.9.3b)

parts:
  U1 = atmega328 [package=dip]
  Part3 = FTDI Basic Programmer
  XTAL1 = Crystal [frequency="16 Mhz" package=THT]
  C1 = Electrolytic Capacitor [capacitance=10μF package="0605 [SMD, electrolytic]"]
  C2 = Ceramic Capacitor [capacitance=22µF package="0603 [SMD, multilayer]"]
  C3 = Ceramic Capacitor [capacitance=22µF package="0603 [SMD, multilayer]"]
  R6 = Resistor [tolerance=±5% resistance=10k package=THT]
  C4 = Ceramic Capacitor [capacitance=100nF package="0603 [SMD, multilayer]"]
  VCC2 = Battery block 9V
  ZS-042_RTC2 = ZS-042 RTC Module
  LED7 = LED - 5mm [color="Green (555nm)" package="5 mm [THT]"]  # not connected
  LED8 = LED - 5mm [color="Yellow (595nm)" package="5 mm [THT]"]  # not connected
  LED9 = LED - 5mm [color="Red (633nm)" package="5 mm [THT]"]  # not connected
  LED10 = LED - 5mm [color="Blue (430nm)" package="5 mm [THT]"]  # not connected
  LED11 = LED - 5mm [color="White (4500K)" package="5 mm [THT]"]  # not connected
  R7 = Resistor [tolerance=±5% resistance=220 package=THT]
  R8 = Resistor [tolerance=±5% resistance=220 package=THT]
  R9 = Resistor [tolerance=±5% resistance=220 package=THT]
  R10 = Resistor [tolerance=±5% resistance=220 package=THT]
  R11 = Resistor [tolerance=±5% resistance=220 package=THT]

nets:
  N1: U1.RESET, R6.Pin_1
  N2: U1.D0_(RX), Part3.TXO
  N3: U1.D1_(TX), Part3.POWER
  N4: U1.XLAT1, C3.1
  N5: U1.XLAT2, XTAL1.pin_0
  N6: U1.D5_(PWM), R7.Pin_0
  N7: U1.D6_(PWM), R8.Pin_0
  N8: U1.D7, R9.Pin_0
  N9: U1.D8, R10.Pin_0
  N10: U1.D12, R11.Pin_0
  N11: U1.GND#21, VCC2.-
  N12: U1.A4, ZS-042_RTC2.SDA
  N13: U1.A5, ZS-042_RTC2.SCL
  N14: Part3.CTS, C4.0
  N15: C1.+, VCC2.+
  N16: C2.1, C3.0
